# Fritzing sketch Unit_1 (saved by Fritzing 1.0.6)

parts:
  U1 = ESP32-38PinWide [part_number=ESP32-38PinWide]
  DS2 = DS18B20 1-Wire Temperature Sensor Probe
  A1 = Arduino pluggable terminal
  A2 = generic ac power supply 4 [package=THT]
  J1 = 220v plug

nets:
  GND: U1.GND, DS2.GND, A1.Pin_3, A1.Pin_4, A2.pin3#2
  VIN: U1.VIN, DS2.VDD, A1.Pin_2, A1.Pin_5, A2.pin3#3
  N1: U1.GPIO4, DS2.DQ, A1.Pin_1, A1.Pin_6
  N2: A2.pin1, J1.pin1
  N3: A2.pin2, J1.pin2

custom parts:
  ESP32-38PinWide: Generic 38-Pin ESP32 with wide format (only access to one side of pins on a breadboard) based on Stephen Lilley's HiLetgo ESP-WROOM-32 ESP32 ESP-32S Development Board.
  Arduino pluggable terminal: Arduino pluggable terminal.
  generic ac power supply 4: Universal input voltage: 85-264V AC or 110-370V DC.
  220v plug: Generic 220V AC plug.
