# Fritzing sketch Unit_2 (saved by Fritzing 1.0.6)

parts:
  U1 = ESP32-38PinWide [part_number=ESP32-38PinWide]
  A1 = generic ac power supply 4 [package=THT]
  A2 = illuminated SPDT push button switch
  o1 = Module display OLED I2C 128x64 SSD1306 [package=THT]
  J1 = 220v plug

nets:
  N1: U1.GPIO14, A2.Pin_2
  N2: U1.GPIO11, A1.pin3#2, A2.Pin_3, A2.Pin_5, o1.GND
  VIN: U1.VIN, A1.pin3#3, A2.Pin_4, o1.VCC
  N3: U1.GPIO21, o1.SDA
  N4: U1.GPIO22, o1.SCL
  N5: A1.pin1, J1.pin1
  N6: A1.pin2, J1.pin2

custom parts:
  ESP32-38PinWide: Generic 38-Pin ESP32 with wide format (only access to one side of pins on a breadboard) based on Stephen Lilley's HiLetgo ESP-WROOM-32 ESP32 ESP-32S Development Board.
  generic ac power supply 4: Universal input voltage: 85-264V AC or 110-370V DC.
  illuminated SPDT push button switch: illuminated SPDT push button switch.
  Module display OLED I2C 128x64 SSD1306: Ecran OLED I2C SSD163 de 128x64 avec connexion I2C
  220v plug: Generic 220V AC plug.
