# Fritzing sketch Unit_3 (saved by Fritzing 1.0.6)

parts:
  U1 = ESP32-38PinWide [part_number=ESP32-38PinWide]
  M1 = 1 chan 5v relay module
  A1 = generic ac power supply 4 [package=THT]
  S1 = Toggle Switch spst [package=THT]
  DS1 = DS18B20 1-Wire Temperature Sensor Probe
  A2 = Arduino pluggable terminal
  o1 = Module display OLED I2C 128x64 SSD1306 [package=THT]
  RE2 = KY-040 Rotary encoder [package="Breakout board"]
  J1 = 230V Outlet
  J2 = 220v plug

nets:
  N1: U1.GPIO25, RE2.CLK
  N2: U1.GPIO26, RE2.DT
  N3: U1.GPIO27, RE2.SW
  GND: U1.GPIO11, M1.pin_2, A1.pin3#2, DS1.GND, A2.Pin_3, A2.Pin_4, o1.GND, RE2.GND
  VCC: U1.VIN, M1.pin_1, S1.L1, DS1.VDD, A2.Pin_2, A2.Pin_5, o1.VCC, RE2.Vcc
  N4: U1.GPIO4, DS1.DQ, A2.Pin_1, A2.Pin_6
  N5: U1.GPIO5, M1.pin_3
  N6: U1.GPIO21, o1.SDA
  N7: U1.GPIO22, o1.SCL
  N8: M1.pin_4, J1.N
  N9: M1.pin_5, A1.pin1, J2.pin1
  N10: A1.pin2, J1.H, J2.pin2
  N11: A1.pin3#3, S1.COM

custom parts:
  ESP32-38PinWide: Generic 38-Pin ESP32 with wide format (only access to one side of pins on a breadboard) based on Stephen Lilley's HiLetgo ESP-WROOM-32 ESP32 ESP-32S Development Board.
  1 chan 5v relay module: 1 Channel 5V Relay Module Board Shield with Optocoupler Support High and Low Level Trigger for Arduino.
  generic ac power supply 4: Universal input voltage: 85-264V AC or 110-370V DC.
  Toggle Switch spst: Toggle Switch single pole single throw
  Arduino pluggable terminal: Arduino pluggable terminal.
  Module display OLED I2C 128x64 SSD1306: Ecran OLED I2C SSD163 de 128x64 avec connexion I2C
  KY-040 Rotary encoder: KY-040 Rotary Encoder with switch on breakout borad from AZ Delivery
  230V Outlet: 230V power outlet. Note that PCB has been suppressed. (vanepp: changed part name from 120V to 230V replaced moduleId removed terminalIds from breadboard in the fzp file and cleaned up svgs changed part label to J from A and changed label to 230V in schematic.)
  220v plug: Generic 220V AC plug.
